// Logisim project 8BitComputer.circ as structural Verilog
module ALU (
  input  [7:0] RegA,
  input  [7:0] RegB,
  input  OE,
  output [7:0] Dout,
  output [7:0] ALUresult,
  output CARRYout
);

  Adder adder_1 (.a(RegA), .b(RegB), .out(ALUresult), .cout(CARRYout));  // open: cin
  assign Dout = OE ? ALUresult : 8'bz;  // Controlled_Buffer controlled_buffer_1

  // Notes on the sheet:
  //   ALU (8bits)
endmodule
